# Fritzing sketch wattmetre (saved by Fritzing 0.9.3b)
breadboards: 1

parts:
  1602_LCD = LCD screen
  Arduino_Uno = Arduino Uno (Rev3)
  Q1 = NPN-Transistor [package="TO92 [THT]"]
  Q2 = NPN-Transistor [package="TO92 [THT]"]
  U1 = RELAY [package=relay-t9a]
  U2 = RELAY [package=relay-t9a]
  10k = TRIMPOT [package=trimpot-3mm-2]
  R1 = Resistor [tolerance=±5% resistance=40k package="1206 [SMD]"]
  R2 = Resistor [tolerance=±5% resistance=10k package="1206 [SMD]"]
  U3 = ACS712 [package=so08]
  R3 = Resistor [tolerance=±5% resistance=220 package="1206 [SMD]"]
  R4 = Resistor [tolerance=±5% resistance=220 package="1206 [SMD]"]
  D1 = SOLAR-IXYS [package=solarbit-12x1]
  R5 = Resistor [tolerance=±5% resistance=10k package="1206 [SMD]"]
  U4 = LIPO-1000mAh [package=lipo-1000]

nets:
  GND: 1602_LCD.VSS, 1602_LCD.LED-, Arduino_Uno.GND, U1.COIL2, U2.COIL2, R2.Pin_1, U3.GND, D1.A, U4.-
  N1: 1602_LCD.VDD, 10k.CW
  N2: 1602_LCD.V0, 10k.WIPER
  N3: 1602_LCD.RS, Arduino_Uno.D12/MISO
  N4: 1602_LCD.R/W, 10k.CCW
  N5: 1602_LCD.E, Arduino_Uno.D11_PWM/MOSI
  N6: 1602_LCD.DB4, Arduino_Uno.D5_PWM
  N7: 1602_LCD.DB5, Arduino_Uno.D4
  N8: 1602_LCD.DB6, Arduino_Uno.D3_PWM
  N9: 1602_LCD.DB7, Arduino_Uno.D2
  N10: 1602_LCD.LED+, R5.Pin_1
  N11: Arduino_Uno.A0, U3.VOUT
  N12: Arduino_Uno.A1, R1.Pin_0
  N13: Arduino_Uno.D6_PWM, R3.Pin_0
  N14: Arduino_Uno.D7, R4.Pin_0
  5V: Arduino_Uno.5V, U3.VCC, R5.Pin_0
  N15: Arduino_Uno.VIN, U1.NC, U4.+
  N16: Q1.E, U2.COIL1
  N17: Q1.B, R3.Pin_1
  N18: Q1.C, Q2.C
  N19: Q2.E, U1.COIL1
  N20: Q2.B, R4.Pin_1
  N21: U1.MAIN, U3.IP-
  N22: U2.MAIN, D1.C
  N23: U2.NC, U3.IP+
  N24: R1.Pin_1, R2.Pin_0
